// Logisim project Lab3.circ as structural Verilog: 1 circuit, main circuit main
module main (
  input  in_1,
  input  in_2,
  input  in_3,
  input  in_4,
  input  in_5,
  input  in_6
);

  wire A0, A1, A2, A3, and_1_out, and_2_out, and_3_out, and_4_out, and_5_out, and_6_out, and_7_out,
       and_8_out, and_9_out, and_10_out, and_11_out, and_12_out, and_13_out, and_14_out, and_15_out,
       and_16_out, and_17_out, clock, D0, D1, D2, D3, j_k_ff_6_qn, j_k_ff_7_qn, j_k_ff_8_qn, nor_1_out,
       not_1_out, not_2_out, not_3_out, not_4_out, not_5_out, not_6_out, not_7_out, not_8_out, not_9_out,
       not_10_out, or_1_out, U0, U1, U2, U3, undriven, undriven_2, xor_1_out, xor_2_out, xor_3_out, xor_4_out;

  J_K_Flip_Flop j_k_ff_1 (.J(and_1_out), .clk(clock), .K(and_1_out), .Q(U3));  // open: Qn, preset, en, reset
  and and_1 (and_1_out, U2, U1, U0);
  not not_1 (not_1_out, in_3);
  not not_2 (not_2_out, in_4);
  not not_3 (not_3_out, in_5);
  not not_4 (not_4_out, in_6);
  xor xor_1 (xor_1_out, A3, in_3);
  not not_5 (not_5_out, xor_1_out);
  not not_6 (not_6_out, xor_2_out);
  xor xor_2 (xor_2_out, A2, in_4);
  not not_7 (not_7_out, xor_3_out);
  xor xor_3 (xor_3_out, A1, in_5);
  xor xor_4 (xor_4_out, A0, in_6);
  not not_8 (not_8_out, xor_4_out);
  J_K_Flip_Flop j_k_ff_2 (.J(and_2_out), .clk(clock), .K(and_2_out), .Q(U2), .reset(undriven));  // open: Qn, preset, en
  and and_2 (and_2_out, U1, U0);
  and and_3 (and_3_out, A3, not_1_out);
  and and_4 (and_4_out, A2, not_5_out, not_2_out);
  and and_5 (and_5_out, not_5_out, A1, not_3_out, not_6_out);
  and and_6 (and_6_out, not_5_out, A0, not_6_out, not_4_out, not_7_out);
  J_K_Flip_Flop j_k_ff_3 (.J(U0), .clk(clock), .K(U0), .Q(U1));  // open: Qn, preset, en, reset
  J_K_Flip_Flop j_k_ff_4 (.J(in_1), .clk(clock), .K(in_1), .Q(U0));  // open: Qn, preset, en, reset
  not not_9 (not_9_out, in_2);
  not not_10 (not_10_out, not_9_out);
  or or_1 (or_1_out, and_3_out, and_4_out, and_5_out, and_6_out);
  and and_7 (and_7_out, not_5_out, not_6_out, not_7_out, not_8_out);
  and and_8 (and_8_out, U3, not_10_out);
  and and_9 (and_9_out, U2, not_10_out);
  and and_10 (and_10_out, D3, not_9_out);
  or or_2 (A3, and_8_out, and_10_out);
  nor nor_1 (nor_1_out, or_1_out, and_7_out);
  Clock clock_1 (.out(clock));
  and and_11 (and_11_out, D2, not_9_out);
  and and_12 (and_12_out, U1, not_10_out);
  or or_3 (A2, and_9_out, and_11_out);
  and and_13 (and_13_out, U0, not_10_out);
  and and_14 (and_14_out, D1, not_9_out);
  or or_4 (A1, and_12_out, and_14_out);
  and and_15 (and_15_out, D0, not_9_out);
  or or_5 (A0, and_13_out, and_15_out);
  J_K_Flip_Flop j_k_ff_5 (.J(and_16_out), .clk(clock), .K(and_16_out), .Q(D3));  // open: Qn, preset, en, reset
  and and_16 (and_16_out, j_k_ff_6_qn, j_k_ff_7_qn, j_k_ff_8_qn);
  J_K_Flip_Flop j_k_ff_6 (
    .J(and_17_out), .clk(clock), .K(and_17_out), .Q(D2), .Qn(j_k_ff_6_qn), .reset(undriven_2));  // open: preset, en
  and and_17 (and_17_out, j_k_ff_7_qn, j_k_ff_8_qn);
  J_K_Flip_Flop j_k_ff_7 (
    .J(j_k_ff_8_qn), .clk(clock), .K(j_k_ff_8_qn), .Q(D1), .Qn(j_k_ff_7_qn));  // open: preset, en, reset
  J_K_Flip_Flop j_k_ff_8 (.J(in_1), .clk(clock), .K(in_1), .Q(D0), .Qn(j_k_ff_8_qn));  // open: preset, en, reset

  // Other names for the same wires on the sheet: B0 = in_6; B1 = in_5; B2 = in_4; B3 = in_3; input = in_1;
  //   select = in_2

  // Notes on the sheet:
  //   UPCOUNTER
  //   4bit COMPARITOR
  //   A>B
  //   A=B
  //   8x4 MUX
  //   A<B
  //   DOWNCOUNTER
  //   4bit Comparison Number
endmodule
