// Logisim project Lab 1.circ as structural Verilog: 1 circuit, main circuit main
module main (
  input  clck,
  input  in_2,
  input  in_3,
  input  clck_2
);

  wire j_k_ff_1_q, j_k_ff_1_qn, j_k_ff_2_qn, t_ff_1_q, t_ff_1_qn, t_ff_2_q, t_ff_2_qn;

  T_Flip_Flop t_ff_1 (.clk(clck), .T(in_2), .Q(t_ff_1_q), .Qn(t_ff_1_qn));  // open: preset, reset, en
  J_K_Flip_Flop j_k_ff_1 (
    .J(in_3), .clk(clck_2), .K(in_3), .Q(j_k_ff_1_q), .Qn(j_k_ff_1_qn));  // open: preset, en, reset
  T_Flip_Flop t_ff_2 (.clk(clck), .T(t_ff_1_q), .Q(t_ff_2_q), .Qn(t_ff_2_qn));  // open: preset, reset, en
  J_K_Flip_Flop j_k_ff_2 (
    .J(j_k_ff_1_q), .clk(clck_2), .K(j_k_ff_1_q), .Qn(j_k_ff_2_qn));  // open: Q, preset, en, reset
  LED UP (.in(j_k_ff_1_qn));
  LED led_1 (.in(j_k_ff_2_qn));
  LED UP_2 (.in(t_ff_2_q));
  LED DOWN (.in(t_ff_2_qn));
  LED led_2 (.in(t_ff_1_q));
  LED led_3 (.in(t_ff_1_qn));
endmodule
